# Fritzing sketch 연결 (saved by Fritzing 0.9.2b)
breadboards: 1

parts:
  부품1 = Arduino Uno (Rev3) - ICSP
  OLED1 = 128x32 I2C Monochrome OLED Display
  U1 = MLX90614 [package=to-39]

nets:
  N1: 부품1.A4/SDA, OLED1.SDA, U1.VSS
  N2: 부품1.A5/SCL, OLED1.SCL, U1.VDD
  3V3: 부품1.3V3, OLED1.3.3V, U1.SCL_VZ
  GND: 부품1.GND, OLED1.GND, U1.PWM_SDA
