# Fritzing sketch connection (saved by Fritzing 0.9.2b)

parts:
  PART1 = ML8511 UV Sensor Breakout [part_number=SEN-12705]
  부품1 = Arduino Uno (Rev3)
  Grove1 = Grove OLED 128x96

nets:
  N1: PART1.EN, 부품1.A1
  N2: PART1.OUT, 부품1.A0
  GND: PART1.GND, 부품1.GND, Grove1.GND
  3.3V: PART1.3.3V, 부품1.3V3
  N3: 부품1.A4/SDA, Grove1.SDA
  N4: 부품1.A5/SCL, Grove1.SCL
  5V: 부품1.5V, Grove1.VCC

custom parts:
  ML8511 UV Sensor Breakout: Description: The ML8511 breakout is an easy to use ultraviolet light sensor. The MP8511 UV Sensor works by outputing an analog signal in relation to the amount of UV light it detects. This breakout can be very handy in creating devices that warn the user of sunburn or detect the UV index as it relates to weather conditions. This sensor breakout can detect 280-390nm light most effectively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
