# Fritzing sketch AVR_TempratureSensor (saved by Fritzing 0.9.2b)
breadboards: 1

parts:
  DS2 = DS18B20 1-Wire Temperature Sensor Probe Cable
  DHT1 = DHT11 Humitidy and Temperature Sensor
  microSD1 = MicroSD Breakout
  부품1 = Arduino Uno (Rev3) - ICSP
  OLED1 = 128x32 I2C Monochrome OLED Display
  R1 = Resistor [tolerance=±5% resistance=1k package=THT]
  R2 = Resistor [tolerance=±5% resistance=1k package=THT]

nets:
  GND: DS2.GND, DHT1.GND, microSD1.GND, 부품1.GND, OLED1.GND
  VDD: DS2.VDD, DHT1.VDD, 부품1.3V3, OLED1.3.3V, R1.Pin_1, R2.Pin_1
  N1: DS2.shield, 부품1.D2, R1.Pin_0
  N2: DHT1.DATA, 부품1.D3_PWM, R2.Pin_0
  N3: microSD1.CS, 부품1.D4
  N4: microSD1.DI, 부품1.D11_PWM/MOSI
  N5: microSD1.DO, 부품1.D12/MISO
  N6: microSD1.CLK, 부품1.D13/SCK
  5V: microSD1.5V, 부품1.5V
  N7: 부품1.A4/SDA, OLED1.SDA
  N8: 부품1.A5/SCL, OLED1.SCL

custom parts:
  DHT11 Humitidy and Temperature Sensor: DHT11 Humidity and Temperature Sensor
  MicroSD Breakout: 5V-ready microSD Breakout with Level Shifter
