# Fritzing sketch AVR_TempratureDustSensorRTCOLEDEthernet (saved by Fritzing 0.9.2b)
breadboards: 1

parts:
  DHT1 = DHT11 Humitidy and Temperature Sensor
  R2 = Resistor [tolerance=±5% resistance=1k package=THT]
  ENC28J1 = ENC28J60
  부품2 = Arduino Mega 2560 (Rev3)
  OLED2 = 128x32 I2C Monochrome OLED Display
  RTC2 = DS1307 RTC Breakout
  U1 = PIC-ICSP [package=molex-1x6]
  R3 = Resistor [tolerance=±5% resistance=150 package=THT]

nets:
  VDD: DHT1.VDD, ENC28J1.3.3, 부품2.3V3, OLED2.3.3V, RTC2.5V
  N1: DHT1.DATA, R2.Pin_0, 부품2.D3_PWM
  GND: DHT1.GND, R2.Pin_1, ENC28J1.GND, 부품2.GND, OLED2.GND, RTC2.GND, U1.PGC, U1.GND
  N2: ENC28J1.INT, ENC28J1.SO, 부품2.D50
  N3: ENC28J1.SCK, ENC28J1.RST, ENC28J1.CS, 부품2.D10_PWM, 부품2.D52
  N4: ENC28J1.SI, 부품2.D51
  N5: 부품2.A0, U1.VCC
  N6: 부품2.SCL, OLED2.SCL
  N7: 부품2.SDA, OLED2.SDA
  N8: 부품2.5V, R3.Pin_0
  N9: 부품2.D6_PWM, U1.PGD
  N10: U1.PGM, R3.Pin_1

custom parts:
  DHT11 Humitidy and Temperature Sensor: DHT11 Humidity and Temperature Sensor
  ENC28J60: Ethernet Module ENC28J60
  DS1307 RTC Breakout: DS1307 Real-time Clock Breakout Board with Battery
