# Fritzing sketch connection (saved by Fritzing 0.9.2b)
breadboards: 1

parts:
  BREAKOUT1 = HMC5883L Compass Breakout
  부품1 = Arduino Uno (Rev3) - ICSP
  R1 = Resistor [tolerance=±5% resistance=220 package=THT]
  R2 = Resistor [tolerance=±5% resistance=220 package=THT]

nets:
  N1: BREAKOUT1.SCL, 부품1.A5/SCL, R1.Pin_0
  N2: BREAKOUT1.SDA, 부품1.A4/SDA, R2.Pin_0
  N3: BREAKOUT1.3vo, 부품1.3V3, R1.Pin_1, R2.Pin_1
  GND: BREAKOUT1.GND, 부품1.GND
