# Fritzing sketch 연결 (saved by Fritzing 0.9.2b)

parts:
  부품1 = Arduino Uno (Rev3)
  S3 = Pushbutton [package="[THT]"]
  Part1 = KY-008 Laser Transmitter Module [package="Breakout board"]
  부품2 = Arduino Uno (Rev3)
  R1 = Resistor [tolerance=±5% resistance=220 package=THT]
  LED1 = LED - 5mm [color="Red (633nm)" package="5 mm [THT]"]

nets:
  N1: 부품1.D13/SCK, Part1.S
  N2: 부품1.GND, S3.Pin_4, Part1.-
  N3: 부품1.D2, S3.Pin_2
  N4: 부품2.D12/MISO, R1.Pin_1
  N5: 부품2.GND, LED1.cathode
  N6: R1.Pin_0, LED1.anode

custom parts:
  KY-008 Laser Transmitter Module: Laser Transmitter module KY-008 for Arduino, emits a dot shaped red laser beam.
