# Fritzing sketch backsoon (saved by Fritzing 0.9.2b)

parts:
  부품1 = Arduino Uno (Rev3) - ICSP
  ENC28J1 = ENC28J60

nets:
  N1: 부품1.D10_PWM/SS, ENC28J1.CS
  N2: 부품1.D11_PWM/MOSI, ENC28J1.SI
  N3: 부품1.D12/MISO, ENC28J1.SO
  N4: 부품1.D13/SCK, ENC28J1.SCK, ENC28J1.RST
  N5: 부품1.3V3, ENC28J1.3.3
  GND: 부품1.GND, ENC28J1.GND

custom parts:
  ENC28J60: Ethernet Module ENC28J60
