# Fritzing sketch Untitled Sketch 2 (saved by Fritzing 0.9.2b)
breadboards: 1

parts:
  RTC1 = DS1307 RTC Breakout
  부품1 = Arduino Mega ADK (Rev3)
  OLED1 = 128x32 I2C Monochrome OLED Display

nets:
  GND: RTC1.GND, 부품1.GND, OLED1.GND
  5V: RTC1.5V, 부품1.5V
  N1: RTC1.SDA, 부품1.D20/SDA, OLED1.SDA
  N2: RTC1.SCL, 부품1.D21/SCL, OLED1.SCL
  3V3: 부품1.3V3, OLED1.3.3V

custom parts:
  DS1307 RTC Breakout: DS1307 Real-time Clock Breakout Board with Battery
