# Fritzing sketch ESP8266Mega (saved by Fritzing 0.9.2b)

parts:
  부품1 = Arduino Mega ADK (Rev3)
  Espessif_Serial_Wifi_Modul_1 = ESP8266 ESP01 [part_number=ESP8266 package=THT]

nets:
  N1: 부품1.D17/RX2, Espessif_Serial_Wifi_Modul_1.TXD
  N2: 부품1.D16/TX2, Espessif_Serial_Wifi_Modul_1.RXD
  3V3: 부품1.3V3, Espessif_Serial_Wifi_Modul_1.VCC
  GND: 부품1.GND, Espessif_Serial_Wifi_Modul_1.GND

custom parts:
  ESP8266 ESP01: Generic WiFi Module based on the ESP8266 with onboard PCB antenna and UART communications
